// Logisim project Z80.circ as structural Verilog: 2 circuits, main circuit main
module main (
  input  [7:0] N,
  input  [7:0] N16
);

  wire adder_2_cout, adder_3_cout, adder_4_cout, adder_5_cout, adder_6_cout, adder_7_cout, adder_8_cout,
       adder_9_cout, and_15_out, and_17_out, and_18_out, and_19_out, and_24_out, and_25_out, and_26_out,
       and_27_out, and_28_out, and_29_out, and_30_out, and_32_out, and_33_out, Carry, CarryIn, Clk,
       controlled_buffer_50_out, controlled_buffer_52_out, GET_DT, H, HIn, IsN, IsN2, JMP, JMP1, JMP2, Ndaa,
       NdaaIn, not_1_out, not_2_out, not_3_out, not_4_out, not_5_out, not_6_out, not_7_out, not_8_out,
       not_9_out, not_10_out, not_11_out, not_12_out, not_13_out, not_14_out, not_15_out, not_16_out,
       not_17_out, not_18_out, not_19_out, not_20_out, not_21_out, not_22_out, not_23_out, not_24_out,
       not_25_out, not_26_out, not_27_out, not_28_out, not_29_out, not_30_out, not_31_out, not_32_out,
       not_33_out, not_34_out, not_35_out, not_36_out, not_37_out, not_38_out, not_39_out, not_40_out,
       not_41_out, not_42_out, not_43_out, not_44_out, not_45_out, not_46_out, not_47_out, not_48_out,
       not_49_out, not_50_out, not_51_out, not_52_out, not_53_out, not_54_out, not_55_out, not_56_out,
       not_57_out, not_58_out, not_59_out, not_60_out, not_61_out, not_62_out, not_63_out, not_64_out,
       not_65_out, not_66_out, not_67_out, o3, or_3_out, or_4_out, P_V, P_VIn, PCwr, Reset, S, SIn,
       subtractor_1_bout, subtractor_2_bout, subtractor_3_bout, subtractor_4_bout, subtractor_5_bout,
       subtractor_6_bout, subtractor_7_bout, subtractor_8_bout, WE, WR, WR1, WR_A, WR_A1, WR_A2, WR_A3,
       WR_A4, WR_A5, WR_A7, WR_A8, WR_A9, WR_A10, WR_A12, WR_A13, WR_ON, Z, ZIn;
  wire [2:0] r, rin;
  wire [5:3] Flags_q;
  wire [7:0] A16in, A16out, adder_2_out, adder_4_out, adder_6_out, adder_7_out, Ain, and_9_out, and_10_out,
       Aout, InstOut, N16_t, N_t, or_5_out, or_6_out, R16_Out, R_Out, RS_OUT, subtractor_1_out,
       subtractor_3_out, subtractor_6_out, subtractor_7_out;
  wire [15:0] adder_1_out, PCin, PCout;

  Clock clock_1 (.out(Clk));
  Button u_R (.out(Reset));
  Register #(.width(16)) A (.D({A16in, Ain}), .en(WR_A), .clk(Clk), .Q({A16out, Aout}), .clr(Reset));
  Register Flags (
    .D({SIn, ZIn, 1'b0, HIn, 1'b0, P_VIn, NdaaIn, CarryIn}), .en(WR_A), .clk(Clk),
    .Q({S, Z, Flags_q[5], H, Flags_q[3], P_V, Ndaa, Carry}));  // open: clr
  or or_1 (JMP, JMP1, JMP2);
  Register Rejestr_Sterujacy (.D(InstOut), .en(WE), .clk(Clk), .Q(RS_OUT), .clr(Reset));
  Register #(.width(16)) N_mem (.D({N16, N}), .en(GET_DT), .clk(Clk), .Q({N16_t, N_t}), .clr(Reset));
  buf or_2 (IsN, IsN2);  // OR_Gate
  Comparator comparator_1 (.a(Ain), .b({8{1'b0}}), .eq(ZIn), .lt(SIn));  // open: gt
  or or_3 (or_3_out, WR_A12, WR_A13, WR_A1, WR_A3, WR_A4, WR_A2, WR_A5, o3, WR_A7, WR_A8, WR_A9, WR_A10);
  Rejestry rejestry_1 (
    .rin(rin), .r(r), .WR(WR), .Clk(Clk), .N(N_t), .IsN(IsN), .WEinst(WE), .PCin(PCin), .WR_PC(PCwr),
    .Reset(Reset), .R_Out(R_Out), .R16_Out(R16_Out), .PC_out(PCout), .InstOut(InstOut));
  or or_4 (or_4_out, WR1, IsN2);
  and and_1 (WR, or_4_out, WR_ON);
  and and_2 (WR_A, or_3_out, WR_ON);
  not not_1 (not_1_out, RS_OUT[3]);
  not not_2 (not_2_out, RS_OUT[4]);
  not not_3 (not_3_out, RS_OUT[6]);
  not not_4 (not_4_out, RS_OUT[0]);
  not not_5 (not_5_out, RS_OUT[3]);
  not not_6 (not_6_out, RS_OUT[4]);
  not not_7 (not_7_out, RS_OUT[3]);
  not not_8 (not_8_out, RS_OUT[6]);
  not not_9 (not_9_out, RS_OUT[0]);
  not not_10 (not_10_out, RS_OUT[3]);
  not not_11 (not_11_out, RS_OUT[0]);
  not not_12 (not_12_out, RS_OUT[6]);
  not not_13 (not_13_out, RS_OUT[7]);
  assign r = WR_A9 ? RS_OUT[2:0] : 3'bz;  // Controlled_Buffer controlled_buffer_1
  and and_3 (WR_A9, not_1_out, not_2_out, RS_OUT[5], not_3_out, RS_OUT[7]);
  and and_4 (WR_A10, not_4_out, RS_OUT[1], RS_OUT[2], not_5_out, not_6_out, RS_OUT[5], RS_OUT[6], RS_OUT[7]);
  assign r = WR_A12 ? RS_OUT[2:0] : 3'bz;  // Controlled_Buffer controlled_buffer_2
  and and_5 (WR_A12, not_7_out, RS_OUT[4], RS_OUT[5], not_8_out, RS_OUT[7]);
  and and_6 (WR_A13, not_9_out, RS_OUT[1], RS_OUT[2], not_10_out, RS_OUT[4], RS_OUT[5], RS_OUT[6], RS_OUT[7]);
  assign rin = WR1 ? RS_OUT[5:3] : 3'bz;  // Controlled_Buffer controlled_buffer_3
  and and_7 (WR1, RS_OUT[6], not_14_out);
  not not_14 (not_14_out, RS_OUT[7]);
  assign A16in = WR_A10 ? A16out : 8'bz;  // Controlled_Buffer controlled_buffer_4
  D_Flip_Flop d_ff_1 (.D(WE), .clk(Clk), .Q(GET_DT), .reset(Reset));  // open: Qn, preset
  assign r = WR1 ? RS_OUT[2:0] : 3'bz;  // Controlled_Buffer controlled_buffer_5
  assign rin = IsN2 ? RS_OUT[5:3] : 3'bz;  // Controlled_Buffer controlled_buffer_6
  and and_8 (IsN2, not_11_out, RS_OUT[1], RS_OUT[2], not_12_out, not_13_out);
  assign r = IsN2 ? 3'b110 : 3'bz;  // Controlled_Buffer controlled_buffer_7
  assign A16in = WR_A9 ? A16out : 8'bz;  // Controlled_Buffer controlled_buffer_8
  assign and_9_out = Aout & R_Out;  // AND_Gate and_9, 8 bits wide
  assign and_10_out = Aout & N_t;  // AND_Gate and_10, 8 bits wide
  assign Ain = WR_A10 ? and_10_out : 8'bz;  // Controlled_Buffer controlled_buffer_9
  assign A16in = WR_A12 ? A16out : 8'bz;  // Controlled_Buffer controlled_buffer_10
  assign or_5_out = Aout | R_Out;  // OR_Gate or_5, 8 bits wide
  assign A16in = WR_A13 ? A16out : 8'bz;  // Controlled_Buffer controlled_buffer_11
  assign or_6_out = Aout | N_t;  // OR_Gate or_6, 8 bits wide
  assign Ain = WR_A13 ? or_6_out : 8'bz;  // Controlled_Buffer controlled_buffer_12
  D_Flip_Flop d_ff_2 (.D(GET_DT), .clk(Clk), .Q(WR_ON), .reset(Reset));  // open: Qn, preset
  assign Ain = WR_A9 ? and_9_out : 8'bz;  // Controlled_Buffer controlled_buffer_13
  assign Ain = WR_A12 ? or_5_out : 8'bz;  // Controlled_Buffer controlled_buffer_14
  assign PCin = not_15_out ? adder_1_out : 16'bz;  // Controlled_Buffer controlled_buffer_15
  Adder #(.width(16)) adder_1 (.a(PCout), .b(16'h1), .out(adder_1_out));  // open: cin, cout
  not not_15 (not_15_out, JMP);
  D_Flip_Flop d_ff_3 (.D(WR_ON), .clk(Clk), .Q(PCwr), .reset(Reset));  // open: Qn, preset
  not not_16 (not_16_out, RS_OUT[3]);
  not not_17 (not_17_out, RS_OUT[5]);
  not not_18 (not_18_out, RS_OUT[6]);
  D_Flip_Flop d_ff_4 (.D(PCwr), .clk(Clk), .Q(WE), .preset(Reset));  // open: Qn, reset
  not not_19 (not_19_out, RS_OUT[3]);
  not not_20 (not_20_out, RS_OUT[4]);
  not not_21 (not_21_out, RS_OUT[5]);
  not not_22 (not_22_out, RS_OUT[6]);
  assign NdaaIn = WR_A1 ? 1'b0 : 1'bz;  // Controlled_Buffer controlled_buffer_16
  not not_23 (not_23_out, RS_OUT[4]);
  not not_24 (not_24_out, RS_OUT[5]);
  not not_25 (not_25_out, RS_OUT[6]);
  assign r = WR_A3 ? RS_OUT[2:0] : 3'bz;  // Controlled_Buffer controlled_buffer_17
  and and_11 (WR_A3, not_16_out, RS_OUT[4], not_17_out, not_18_out, RS_OUT[7]);
  assign r = WR_A4 ? RS_OUT[2:0] : 3'bz;  // Controlled_Buffer controlled_buffer_18
  not not_26 (not_26_out, RS_OUT[5]);
  and and_12 (WR_A4, RS_OUT[3], RS_OUT[4], not_26_out, not_27_out, RS_OUT[7]);
  not not_27 (not_27_out, RS_OUT[6]);
  assign r = WR_A1 ? RS_OUT[2:0] : 3'bz;  // Controlled_Buffer controlled_buffer_19
  and and_13 (WR_A1, not_19_out, not_20_out, not_21_out, not_22_out, RS_OUT[7]);
  assign r = WR_A2 ? RS_OUT[2:0] : 3'bz;  // Controlled_Buffer controlled_buffer_20
  and and_14 (WR_A2, RS_OUT[3], not_23_out, not_24_out, not_25_out, RS_OUT[7]);
  assign NdaaIn = WR_A2 ? 1'b0 : 1'bz;  // Controlled_Buffer controlled_buffer_21
  assign NdaaIn = WR_A3 ? 1'b1 : 1'bz;  // Controlled_Buffer controlled_buffer_22
  assign NdaaIn = WR_A4 ? 1'b1 : 1'bz;  // Controlled_Buffer controlled_buffer_23
  not not_28 (not_28_out, RS_OUT[2]);
  not not_29 (not_29_out, RS_OUT[3]);
  not not_30 (not_30_out, RS_OUT[4]);
  not not_31 (not_31_out, RS_OUT[5]);
  assign A16in = WR_A1 ? A16out : 8'bz;  // Controlled_Buffer controlled_buffer_24
  Adder adder_2 (.a(R_Out), .b(Aout), .out(adder_2_out), .cout(adder_2_cout));  // open: cin
  not not_32 (not_32_out, Aout[7]);
  not not_33 (not_33_out, R_Out[7]);
  and and_15 (and_15_out, not_32_out, not_33_out, Ain[7]);
  Adder #(.width(4)) adder_3 (.a(Aout[3:0]), .b(R_Out[3:0]), .cout(adder_3_cout));  // open: out, cin
  assign HIn = WR_A1 ? adder_3_cout : 1'bz;  // Controlled_Buffer controlled_buffer_25
  and and_16 (JMP1, RS_OUT[0], RS_OUT[1], not_28_out, not_29_out, not_30_out, not_31_out, RS_OUT[6], RS_OUT[7]);
  assign Ain = WR_A1 ? adder_2_out : 8'bz;  // Controlled_Buffer controlled_buffer_26
  assign CarryIn = WR_A1 ? adder_2_cout : 1'bz;  // Controlled_Buffer controlled_buffer_27
  assign P_VIn = WR_A1 ? and_15_out : 1'bz;  // Controlled_Buffer controlled_buffer_28
  assign A16in = WR_A2 ? A16out : 8'bz;  // Controlled_Buffer controlled_buffer_29
  assign Ain = WR_A2 ? adder_4_out : 8'bz;  // Controlled_Buffer controlled_buffer_30
  Adder adder_4 (.a(R_Out), .b(Aout), .out(adder_4_out), .cin(Carry), .cout(adder_4_cout));
  assign CarryIn = WR_A2 ? adder_4_cout : 1'bz;  // Controlled_Buffer controlled_buffer_31
  not not_34 (not_34_out, Aout[7]);
  not not_35 (not_35_out, R_Out[7]);
  and and_17 (and_17_out, not_34_out, not_35_out, Ain[7]);
  Adder #(.width(4)) adder_5 (.a(Aout[3:0]), .b(R_Out[3:0]), .cout(adder_5_cout));  // open: out, cin
  assign HIn = WR_A2 ? adder_5_cout : 1'bz;  // Controlled_Buffer controlled_buffer_32
  assign A16in = WR_A3 ? A16out : 8'bz;  // Controlled_Buffer controlled_buffer_33
  Subtractor subtractor_1 (.a(R_Out), .b(Aout), .out(subtractor_1_out), .bout(subtractor_1_bout));  // open: bin
  not not_36 (not_36_out, Aout[7]);
  not not_37 (not_37_out, Ain[7]);
  Subtractor #(.width(4)) subtractor_2 (.a(R_Out[3:0]), .b(Aout[3:0]), .bout(subtractor_2_bout));  // open: out, bin
  assign HIn = WR_A3 ? subtractor_2_bout : 1'bz;  // Controlled_Buffer controlled_buffer_34
  assign A16in = WR_A4 ? A16out : 8'bz;  // Controlled_Buffer controlled_buffer_35
  Subtractor subtractor_3 (.a(R_Out), .b(Aout), .out(subtractor_3_out), .bin(Carry), .bout(subtractor_3_bout));
  not not_38 (not_38_out, Aout[7]);
  not not_39 (not_39_out, Ain[7]);
  Subtractor #(.width(4)) subtractor_4 (.a(R_Out[3:0]), .b(Aout[3:0]), .bout(subtractor_4_bout));  // open: out, bin
  assign HIn = WR_A4 ? subtractor_4_bout : 1'bz;  // Controlled_Buffer controlled_buffer_36
  assign r = JMP1 ? 3'b110 : 3'bz;  // Controlled_Buffer controlled_buffer_37
  assign P_VIn = WR_A2 ? and_17_out : 1'bz;  // Controlled_Buffer controlled_buffer_38
  assign Ain = WR_A3 ? subtractor_1_out : 8'bz;  // Controlled_Buffer controlled_buffer_39
  assign CarryIn = WR_A3 ? subtractor_1_bout : 1'bz;  // Controlled_Buffer controlled_buffer_40
  and and_18 (and_18_out, R_Out[7], not_36_out, not_37_out);
  assign P_VIn = WR_A3 ? and_18_out : 1'bz;  // Controlled_Buffer controlled_buffer_41
  assign Ain = WR_A4 ? subtractor_3_out : 8'bz;  // Controlled_Buffer controlled_buffer_42
  assign CarryIn = WR_A4 ? subtractor_3_bout : 1'bz;  // Controlled_Buffer controlled_buffer_43
  and and_19 (and_19_out, R_Out[7], not_38_out, not_39_out);
  assign P_VIn = WR_A4 ? and_19_out : 1'bz;  // Controlled_Buffer controlled_buffer_44
  assign PCin = JMP1 ? {N16_t, N_t} : 16'bz;  // Controlled_Buffer controlled_buffer_45
  not not_40 (not_40_out, RS_OUT[0]);
  not not_41 (not_41_out, RS_OUT[3]);
  not not_42 (not_42_out, RS_OUT[4]);
  not not_43 (not_43_out, RS_OUT[5]);
  not not_44 (not_44_out, RS_OUT[0]);
  not not_45 (not_45_out, RS_OUT[4]);
  not not_46 (not_46_out, RS_OUT[5]);
  not not_47 (not_47_out, RS_OUT[0]);
  not not_48 (not_48_out, RS_OUT[2]);
  and and_20 (WR_A5, not_40_out, RS_OUT[1], RS_OUT[2], not_41_out, not_42_out, not_43_out, RS_OUT[6], RS_OUT[7]);
  assign NdaaIn = WR_A5 ? 1'b0 : 1'bz;  // Controlled_Buffer controlled_buffer_46
  and and_21 (o3, not_44_out, RS_OUT[1], RS_OUT[2], RS_OUT[3], not_45_out, not_46_out, RS_OUT[6], RS_OUT[7]);
  assign NdaaIn = o3 ? 1'b0 : 1'bz;  // Controlled_Buffer controlled_buffer_47
  not not_49 (not_49_out, RS_OUT[0]);
  not not_50 (not_50_out, RS_OUT[3]);
  not not_51 (not_51_out, RS_OUT[5]);
  assign NdaaIn = WR_A7 ? 1'b1 : 1'bz;  // Controlled_Buffer controlled_buffer_48
  not not_52 (not_52_out, RS_OUT[0]);
  not not_53 (not_53_out, RS_OUT[5]);
  not not_54 (not_54_out, RS_OUT[4]);
  not not_55 (not_55_out, RS_OUT[5]);
  not not_56 (not_56_out, RS_OUT[4]);
  not not_57 (not_57_out, RS_OUT[5]);
  and and_22 (WR_A7, not_49_out, RS_OUT[1], RS_OUT[2], not_50_out, RS_OUT[4], not_51_out, RS_OUT[6], RS_OUT[7]);
  and and_23 (WR_A8, not_52_out, RS_OUT[1], RS_OUT[2], RS_OUT[3], RS_OUT[4], not_53_out, RS_OUT[6], RS_OUT[7]);
  assign NdaaIn = WR_A8 ? 1'b1 : 1'bz;  // Controlled_Buffer controlled_buffer_49
  not not_58 (not_58_out, RS_OUT[3]);
  assign controlled_buffer_50_out = RS_OUT[3] ? controlled_buffer_52_out : 1'bz;  // Controlled_Buffer controlled_buffer_50
  not not_59 (not_59_out, controlled_buffer_52_out);
  assign controlled_buffer_50_out = not_58_out ? not_59_out : 1'bz;  // Controlled_Buffer controlled_buffer_51
  and and_24 (and_24_out, RS_OUT[4], RS_OUT[5]);
  assign controlled_buffer_52_out = and_25_out ? P_V : 1'bz;  // Controlled_Buffer controlled_buffer_52
  and and_25 (and_25_out, not_54_out, RS_OUT[5]);
  assign controlled_buffer_52_out = and_26_out ? Carry : 1'bz;  // Controlled_Buffer controlled_buffer_53
  and and_26 (and_26_out, RS_OUT[4], not_55_out);
  assign controlled_buffer_52_out = and_27_out ? Z : 1'bz;  // Controlled_Buffer controlled_buffer_54
  and and_27 (and_27_out, not_56_out, not_57_out);
  assign A16in = WR_A5 ? A16out : 8'bz;  // Controlled_Buffer controlled_buffer_55
  assign A16in = o3 ? A16out : 8'bz;  // Controlled_Buffer controlled_buffer_56
  Adder adder_6 (.a(N_t), .b(Aout), .out(adder_6_out), .cin(Carry), .cout(adder_6_cout));
  not not_60 (not_60_out, Aout[7]);
  not not_61 (not_61_out, N_t[7]);
  Subtractor #(.width(4)) subtractor_5 (.a(N_t[3:0]), .b(Aout[3:0]), .bout(subtractor_5_bout));  // open: out, bin
  and and_28 (and_28_out, not_47_out, RS_OUT[1], not_48_out, RS_OUT[6], RS_OUT[7]);
  assign controlled_buffer_52_out = and_24_out ? S : 1'bz;  // Controlled_Buffer controlled_buffer_57
  assign Ain = WR_A5 ? adder_7_out : 8'bz;  // Controlled_Buffer controlled_buffer_58
  Adder adder_7 (.a(N_t), .b(Aout), .out(adder_7_out), .cout(adder_7_cout));  // open: cin
  assign CarryIn = WR_A5 ? adder_7_cout : 1'bz;  // Controlled_Buffer controlled_buffer_59
  not not_62 (not_62_out, Aout[7]);
  not not_63 (not_63_out, N_t[7]);
  and and_29 (and_29_out, not_62_out, not_63_out, Ain[7]);
  Adder #(.width(4)) adder_8 (.a(Aout[3:0]), .b(N_t[3:0]), .cout(adder_8_cout));  // open: out, cin
  assign HIn = WR_A5 ? adder_8_cout : 1'bz;  // Controlled_Buffer controlled_buffer_60
  assign Ain = o3 ? adder_6_out : 8'bz;  // Controlled_Buffer controlled_buffer_61
  assign CarryIn = o3 ? adder_6_cout : 1'bz;  // Controlled_Buffer controlled_buffer_62
  and and_30 (and_30_out, not_60_out, not_61_out, Ain[7]);
  assign P_VIn = o3 ? and_30_out : 1'bz;  // Controlled_Buffer controlled_buffer_63
  Adder #(.width(4)) adder_9 (.a(Aout[3:0]), .b(N_t[3:0]), .cout(adder_9_cout));  // open: out, cin
  assign HIn = o3 ? adder_9_cout : 1'bz;  // Controlled_Buffer controlled_buffer_64
  assign A16in = WR_A7 ? A16out : 8'bz;  // Controlled_Buffer controlled_buffer_65
  Subtractor subtractor_6 (.a(N_t), .b(Aout), .out(subtractor_6_out), .bin(Carry), .bout(subtractor_6_bout));
  assign CarryIn = WR_A7 ? subtractor_6_bout : 1'bz;  // Controlled_Buffer controlled_buffer_66
  not not_64 (not_64_out, Aout[7]);
  not not_65 (not_65_out, Ain[7]);
  assign HIn = WR_A7 ? subtractor_5_bout : 1'bz;  // Controlled_Buffer controlled_buffer_67
  assign A16in = WR_A8 ? A16out : 8'bz;  // Controlled_Buffer controlled_buffer_68
  Subtractor subtractor_7 (.a(N_t), .b(Aout), .out(subtractor_7_out), .bin(Carry), .bout(subtractor_7_bout));
  not not_66 (not_66_out, Aout[7]);
  not not_67 (not_67_out, Ain[7]);
  Subtractor #(.width(4)) subtractor_8 (.a(N_t[3:0]), .b(Aout[3:0]), .bout(subtractor_8_bout));  // open: out, bin
  assign HIn = WR_A8 ? subtractor_8_bout : 1'bz;  // Controlled_Buffer controlled_buffer_69
  and and_31 (JMP2, and_28_out, controlled_buffer_50_out);
  assign r = JMP2 ? 3'b110 : 3'bz;  // Controlled_Buffer controlled_buffer_70
  assign P_VIn = WR_A5 ? and_29_out : 1'bz;  // Controlled_Buffer controlled_buffer_71
  assign Ain = WR_A7 ? subtractor_6_out : 8'bz;  // Controlled_Buffer controlled_buffer_72
  and and_32 (and_32_out, N_t[7], not_64_out, not_65_out);
  assign P_VIn = WR_A7 ? and_32_out : 1'bz;  // Controlled_Buffer controlled_buffer_73
  assign Ain = WR_A8 ? subtractor_7_out : 8'bz;  // Controlled_Buffer controlled_buffer_74
  assign CarryIn = WR_A8 ? subtractor_7_bout : 1'bz;  // Controlled_Buffer controlled_buffer_75
  and and_33 (and_33_out, N_t[7], not_66_out, not_67_out);
  assign P_VIn = WR_A8 ? and_33_out : 1'bz;  // Controlled_Buffer controlled_buffer_76
  assign PCin = JMP2 ? {N16_t, N_t} : 16'bz;  // Controlled_Buffer controlled_buffer_77

  // Other names for the same wires on the sheet: Result[7:0] = Ain; o2 = IsN2; WR2 = IsN2; WR_A6 = o3

  // Notes on the sheet:
  //   ZS_Check
  //   LD
  //   R -> R
  //   N -> R
  //   LD
  //   AND
  //   AND
  //   OR
  //   OR
  //   A -> A and r
  //   A -> A and N
  //   A -> A or r
  //   A -> A or N
  //   ADD A->A+R
  //   ADC A -> A+R+C
  //   SUB A->A-R
  //   SBC A->A-R-C
  //   JP nn
  //   ADD A->A+N
  //   ADC A->A+N+C
  //   SBC A -> A-N-C
  //   SUB A->A-N
  //   JP ccc nn
endmodule

module Rejestry (
  input  [2:0] rin,
  input  [2:0] r,
  input  WR,
  input  Clk,
  input  [7:0] N,
  input  IsN,
  input  WEinst,
  input  [15:0] PCin,
  input  WR_PC,
  input  Reset,
  output [7:0] R_Out,
  output [7:0] R16_Out,
  output [15:0] PC_out,
  output [7:0] InstOut
);

  wire controlled_buffer_5_out, decoder_1_out0, decoder_1_out1, decoder_1_out2, decoder_1_out3,
       decoder_1_out4, decoder_1_out5, decoder_1_out6, decoder_1_out7, not_1_out, not_2_out, not_3_out, WR_A,
       WR_B, WR_C, WR_D, WR_E, WR_H, WR_L, WRram;
  wire [7:0] controlled_buffer_11_out, controlled_buffer_12_out, DataBitsOut, R_Aout, R_Bout, R_Cout, R_Dout,
       R_Eout, R_Hout, R_In, R_Lout;
  wire [15:0] AddressBits;

  Register R_A (.D(R_In), .en(WR_A), .clk(Clk), .Q(R_Aout), .clr(Reset));
  Register R_B (.D(R_In), .en(WR_B), .clk(Clk), .Q(R_Bout), .clr(Reset));
  Register R_C (.D(R_In), .en(WR_C), .clk(Clk), .Q(R_Cout), .clr(Reset));
  assign R_Out = decoder_1_out0 ? R_Bout : 8'bz;  // Controlled_Buffer controlled_buffer_1
  Decoder #(.select(3)) decoder_1 (
    .out0(decoder_1_out0), .out1(decoder_1_out1), .out2(decoder_1_out2), .out3(decoder_1_out3),
    .out4(decoder_1_out4), .out5(decoder_1_out5), .out6(decoder_1_out6), .out7(decoder_1_out7), .sel(r));  // open: en
  assign R_Out = decoder_1_out1 ? R_Cout : 8'bz;  // Controlled_Buffer controlled_buffer_2
  assign R_Out = decoder_1_out2 ? R_Dout : 8'bz;  // Controlled_Buffer controlled_buffer_3
  not not_1 (not_1_out, IsN);
  Register R_D (.D(R_In), .en(WR_D), .clk(Clk), .Q(R_Dout), .clr(Reset));
  Register R_E (.D(R_In), .en(WR_E), .clk(Clk), .Q(R_Eout), .clr(Reset));
  Register R_H (.D(R_In), .en(WR_H), .clk(Clk), .Q(R_Hout), .clr(Reset));
  assign R_Out = decoder_1_out3 ? R_Eout : 8'bz;  // Controlled_Buffer controlled_buffer_4
  assign controlled_buffer_5_out = not_1_out ? decoder_1_out6 : 1'bz;  // Controlled_Buffer controlled_buffer_5
  assign R_In = not_2_out ? R_Out : 8'bz;  // Controlled_Buffer controlled_buffer_6
  not not_2 (not_2_out, IsN);
  assign R_In = IsN ? N : 8'bz;  // Controlled_Buffer controlled_buffer_7
  assign R_Out = decoder_1_out4 ? R_Hout : 8'bz;  // Controlled_Buffer controlled_buffer_8
  assign R_Out = decoder_1_out5 ? R_Lout : 8'bz;  // Controlled_Buffer controlled_buffer_9
  assign R_Out = decoder_1_out7 ? R_Aout : 8'bz;  // Controlled_Buffer controlled_buffer_10
  assign controlled_buffer_11_out = controlled_buffer_5_out ? R_Hout : 8'bz;  // Controlled_Buffer controlled_buffer_11
  assign controlled_buffer_12_out = controlled_buffer_5_out ? R_Lout : 8'bz;  // Controlled_Buffer controlled_buffer_12
  assign R_Out = controlled_buffer_5_out ? DataBitsOut : 8'bz;  // Controlled_Buffer controlled_buffer_13
  Register R_L (.D(R_In), .en(WR_L), .clk(Clk), .Q(R_Lout), .clr(Reset));
  RAM #(.addrWidth(16), .enables("line"), .\type ("nonvolatile")) ram_1 (
    .addr(AddressBits), .we(WRram), .clk(Clk), .din(R_In), .dout(DataBitsOut));
  Demultiplexer #(.select(3)) demultiplexer_1 (
    .out0(WR_B), .out1(WR_C), .out2(WR_D), .out3(WR_E), .out4(WR_H), .out5(WR_L), .out6(WRram), .out7(WR_A),
    .in(WR), .sel(rin));
  assign AddressBits = not_3_out ? {controlled_buffer_12_out, controlled_buffer_11_out} : 16'bz;  // Controlled_Buffer controlled_buffer_14
  not not_3 (not_3_out, WEinst);
  assign AddressBits = WEinst ? PC_out : 16'bz;  // Controlled_Buffer controlled_buffer_15
  assign InstOut = WEinst ? DataBitsOut : 8'bz;  // Controlled_Buffer controlled_buffer_16
  Register #(.width(16)) PC (.D(PCin), .en(WR_PC), .clk(Clk), .Q(PC_out), .clr(Reset));
endmodule
